# Fritzing sketch Sensors Controller (saved by Fritzing 0.9.4)
breadboards: 1

parts:
  WeMos_D1_Mini1 = WeMos D1 Mini
  HC-SR04_Sensor_1 = HC-SR04 Ultrasonic Distance Sensor
  DS1 = DS18B20 1-Wire Temperature Sensor [part_number=DS18B20]
  DS2 = DS18B20 1-Wire Temperature Sensor [part_number=DS18B20]
  DS3 = DS18B20 1-Wire Temperature Sensor [part_number=DS18B20]
  R1 = Resistor [tolerance=±5% resistance=1k package=THT]
  R2 = Resistor [tolerance=±5% resistance=100 package="2010 [SMD]"]
  R3 = Resistor [tolerance=±5% resistance=100 package="2010 [SMD]"]
  R4 = Resistor [tolerance=±5% resistance=2.2k package=THT]

nets (from the schematic view):
  3.3V/PH VCC: WeMos_D1_Mini1.3V3, DS1.VDD, DS2.VDD, DS3.VDD
  5V: WeMos_D1_Mini1.5V, HC-SR04_Sensor_1.VCC
  PH AOUT: WeMos_D1_Mini1.A0
  N1: WeMos_D1_Mini1.D5, DS1.DQ, DS2.DQ, DS3.DQ
  N2: WeMos_D1_Mini1.D6, R3.Pin_1
  N3: WeMos_D1_Mini1.D7, HC-SR04_Sensor_1.TRIG
  GND/PH GND: WeMos_D1_Mini1.G, HC-SR04_Sensor_1.ECHO, DS1.GND, DS2.GND, DS3.GND, R4.Pin_0
  N4: HC-SR04_Sensor_1.GND, R1.Pin_0, R4.Pin_1
  N5: R1.Pin_1, R2.Pin_0
  N6: R2.Pin_1, R3.Pin_0
